// Logisim project Circuit.circ as structural Verilog
module Full_Adder (
  input  X,
  input  Y,
  input  Z,
  output S,
  output C
);

  wire and_1_out, and_2_out, xor_1_out;

  xor xor_1 (xor_1_out, X, Y);
  xor xor_2 (S, xor_1_out, Z);
  and and_1 (and_1_out, X, Y);
  and and_2 (and_2_out, xor_1_out, Z);
  or or_1 (C, and_1_out, and_2_out);
endmodule

module _7483_4_bit_binary_adder (
  input  A1,
  input  B1,
  input  _0,
  input  A2,
  input  B2,
  input  A3,
  input  B3,
  input  A4,
  input  B4,
  input  Vcc,
  input  GRND,
  output S1,
  output S2,
  output S3,
  output S4,
  output Carry
);

  wire full_adder_1_c, full_adder_2_c, full_adder_3_c;

  Full_Adder full_adder_1 (.X(A1), .Y(B1), .Z(_0), .S(S1), .C(full_adder_1_c));
  Full_Adder full_adder_2 (.X(A2), .Y(B2), .Z(full_adder_1_c), .S(S2), .C(full_adder_2_c));
  Full_Adder full_adder_3 (.X(A3), .Y(B3), .Z(full_adder_2_c), .S(S3), .C(full_adder_3_c));
  Full_Adder full_adder_4 (.X(A4), .Y(B4), .Z(full_adder_3_c), .S(S4), .C(Carry));
endmodule
