// Logisim project Lab4.circ as structural Verilog: 1 circuit, main circuit main
module main (
  input  W,
  input  X,
  input  Y,
  input  Z,
  output A,
  output B,
  output C,
  output D
);

  wire and_1_out, and_2_out, and_3_out, and_4_out, and_5_out, not_1_out, not_2_out, or_1_out;

  not not_1 (not_1_out, X);
  not not_2 (not_2_out, Y);
  not not_3 (D, Z);
  or or_1 (or_1_out, Y, Z);
  and and_1 (and_1_out, or_1_out, X);
  or or_2 (A, and_1_out, W);
  and and_2 (and_2_out, or_1_out, X);
  or or_3 (B, and_2_out, and_3_out);
  and and_3 (and_3_out, X, not_2_out, D);
  and and_4 (and_4_out, not_2_out, D);
  or or_4 (C, and_4_out, and_5_out);
  and and_5 (and_5_out, Y, Z);

  // Notes on the sheet:
  //   MD. Musfikur Rahman Roudro
  //   ID-1911849642
endmodule
