// Logisim project Lab5_1.circ as structural Verilog: 1 circuit, main circuit main
module main (
  input  A4,
  input  A3,
  input  A2,
  input  A1,
  input  B4,
  input  B3,
  input  B2,
  input  B1,
  input  C0,
  output Output_carry,
  output S4,
  output S3,
  output S2,
  output S1
);

  wire undriven, xor_1_out, xor_2_out, xor_3_out, xor_4_out;

  xor xor_1 (xor_1_out, B4, C0);
  xor xor_2 (xor_2_out, B3, C0);
  xor xor_3 (xor_3_out, B2, C0);
  xor xor_4 (xor_4_out, B1, C0);
  _7483_4_bit_binary_adder u_7483_4_bit_binary_adder_1 (
    .A1(A1), .B1(xor_4_out), ._0(C0), .A2(A2), .B2(xor_3_out), .A3(A3), .B3(xor_2_out), .A4(A4),
    .B4(xor_1_out), .S1(S1), .S2(S2), .S3(S3), .S4(S4), .Carry(Output_carry), .Vcc(undriven), .GRND(1'b0));

  // Notes on the sheet:
  //   Mode Select M
  //   M = 0 for add
  //   M = 1 for subtract
  //   VCC
  //   Figure: 4-bit adder-subtractor
  //   MD. Musfikur Rahman Roudro
  //   ID-1911849642
endmodule
