// Logisim project Lab5_2.circ as structural Verilog: 1 circuit, main circuit main
module main (
  input  in_1,
  input  A4,
  input  A3,
  input  A2,
  input  A1,
  input  B4,
  input  B3,
  input  B2,
  input  B1,
  input  Ce_0,
  input  Ce_0_2,
  output Carry_Ignored,
  output S4,
  output S3,
  output S2,
  output S1
);

  wire and_1_out, and_2_out, n7483_4_bit_binary_adder_1_carry, n7483_4_bit_binary_adder_1_s1,
       n7483_4_bit_binary_adder_1_s2, n7483_4_bit_binary_adder_1_s3, n7483_4_bit_binary_adder_1_s4, or_1_out,
       or_2_out, undriven, undriven_2;

  _7483_4_bit_binary_adder u_7483_4_bit_binary_adder_1 (
    .A1(A1), .B1(B1), ._0(Ce_0_2), .A2(A2), .B2(B2), .A3(A3), .B3(B3), .A4(A4), .B4(B4),
    .S1(n7483_4_bit_binary_adder_1_s1), .S2(n7483_4_bit_binary_adder_1_s2),
    .S3(n7483_4_bit_binary_adder_1_s3), .S4(n7483_4_bit_binary_adder_1_s4),
    .Carry(n7483_4_bit_binary_adder_1_carry), .Vcc(undriven), .GRND(1'b0));
  or or_1 (or_1_out, n7483_4_bit_binary_adder_1_carry, or_2_out);
  or or_2 (or_2_out, and_1_out, and_2_out);
  and and_1 (and_1_out, n7483_4_bit_binary_adder_1_s4, n7483_4_bit_binary_adder_1_s3);
  and and_2 (and_2_out, n7483_4_bit_binary_adder_1_s4, n7483_4_bit_binary_adder_1_s2);
  _7483_4_bit_binary_adder u_7483_4_bit_binary_adder_2 (
    .A1(in_1), .B1(n7483_4_bit_binary_adder_1_s1), ._0(Ce_0), .A2(or_1_out),
    .B2(n7483_4_bit_binary_adder_1_s2), .A3(or_1_out), .B3(n7483_4_bit_binary_adder_1_s3), .A4(in_1),
    .B4(n7483_4_bit_binary_adder_1_s4), .S1(S1), .S2(S2), .S3(S3), .S4(S4), .Carry(Carry_Ignored),
    .Vcc(undriven_2), .GRND(1'b0));

  // Notes on the sheet:
  //   VCC
  //   K
  //   S4
  //   S3
  //   S2
  //   S1
  //   Figure: BCD adder
  //   A4
  //   A3
  //   A2
  //   A1
  //   B4
  //   B3
  //   B2
  //   B1
  //   VCC
  //   MD. Musfikur Rahman Roudro
  //   ID-1911849642
endmodule
