// Logisim project Lab6.circ as structural Verilog: 1 circuit, main circuit main
module main (
  input  in_1,
  input  in_2,
  input  [1:0] in_3,
  input  in_4,
  output out_5
);

  Multiplexer #(.select(2)) multiplexer_1 (
    .in0(in_1), .in1(in_2), .in2(in_4), .in3(in_4), .out(out_5), .sel(in_3));  // open: en

  // Notes on the sheet:
  //   MD. Musfikur Rahman Roudro
  //   ID-1911849642
endmodule
