// Logisim project Lab7.circ as structural Verilog: 1 circuit, main circuit main
module main (
  input  K,
  input  J,
  output Q,
  output Q_prime
);

  wire and_1_out, and_2_out, clock_1_out;

  Clock clock_1 (.out(clock_1_out));
  and and_1 (and_1_out, Q, K, clock_1_out);
  and and_2 (and_2_out, clock_1_out, J, Q_prime);
  nor nor_1 (Q, and_1_out, Q_prime);
  nor nor_2 (Q_prime, Q, and_2_out);

  // Notes on the sheet:
  //   Clock
  //   Pulse
  //   Figure: J-K Flip-Flop using AND & NOR gates
  //   MD. Musfikur Rahman Roudro
  //   1911849642
endmodule
