// Logisim project Lab8.circ as structural Verilog: 1 circuit, main circuit main
module main (
  input  in_1,
  input  in_2,
  input  in_3,
  output out_4,
  output out_5,
  output out_6,
  output out_7,
  output out_8,
  output out_9,
  output out_10,
  output out_11,
  output out_12,
  output out_13,
  output out_14,
  output out_15
);

  wire and_1_out, and_2_out, and_3_out, and_4_out, clock_1_out, clock_2_out, clock_3_out, not_1_out,
       not_2_out, not_3_out, or_1_out, xor_1_out;

  Clock clock_1 (.out(clock_1_out));
  not not_1 (not_1_out, in_1);
  and and_1 (and_1_out, out_9, not_1_out);
  J_K_Flip_Flop j_k_ff_1 (.J(in_1), .clk(clock_1_out), .K(in_1), .Q(out_6), .Qn(out_9));  // open: preset, en, reset
  J_K_Flip_Flop j_k_ff_2 (
    .J(and_1_out), .clk(clock_1_out), .K(in_1), .Q(out_10), .Qn(out_13));  // open: preset, en, reset
  not not_2 (not_2_out, in_2);
  Clock clock_2 (.out(clock_2_out));
  D_Flip_Flop d_ff_1 (.clk(clock_2_out), .D(xor_1_out), .Q(out_4), .Qn(out_7));  // open: preset, en, reset
  xor xor_1 (xor_1_out, out_4, in_2);
  D_Flip_Flop d_ff_2 (.clk(clock_2_out), .D(and_2_out), .Q(out_11), .Qn(out_14));  // open: preset, en, reset
  and and_2 (and_2_out, out_7, not_2_out);
  not not_3 (not_3_out, in_3);
  and and_3 (and_3_out, out_12, in_3);
  and and_4 (and_4_out, out_8, not_3_out, out_15);
  Clock clock_3 (.out(clock_3_out));
  or or_1 (or_1_out, and_3_out, and_4_out);
  T_Flip_Flop t_ff_1 (.clk(clock_3_out), .T(in_3), .Q(out_5), .Qn(out_8));  // open: preset, reset, en
  T_Flip_Flop t_ff_2 (.clk(clock_3_out), .T(or_1_out), .Q(out_12), .Qn(out_15));  // open: preset, reset, en

  // Notes on the sheet:
  //   Sequential Circuit using J-K Flip-Flop
  //   Sequential Circuit using D Flip-Flop
  //   MD. Musfikur Rahman Roudro
  //   ID-1911849642
  //   Sequential Circuit using T Flip-Flop
endmodule
