// Logisim project test.circ as structural Verilog: 3 circuits, main circuit main
module main (
  input  X,
  input  Y,
  input  Z,
  output S,
  output C
);

  wire and_1_out, and_2_out, xor_1_out;

  xor xor_1 (xor_1_out, X, Y);
  xor xor_2 (S, xor_1_out, Z);
  and and_1 (and_1_out, X, Y);
  and and_2 (and_2_out, xor_1_out, Z);
  or or_1 (C, and_1_out, and_2_out);
endmodule

module Adder (
  input  X,
  input  Y,
  input  Z,
  output S,
  output C
);

  wire and_1_out, and_2_out, xor_1_out;

  xor xor_1 (xor_1_out, X, Y);
  xor xor_2 (S, xor_1_out, Z);
  and and_1 (and_1_out, X, Y);
  and and_2 (and_2_out, xor_1_out, Z);
  or or_1 (C, and_1_out, and_2_out);
endmodule

module IC_7483 (
  input  A1,
  input  B1,
  input  _0,
  input  A2,
  input  B2,
  input  A3,
  input  B3,
  input  A4,
  input  B4,
  input  Vcc,
  input  GRND,
  output S1,
  output S2,
  output S3,
  output S4,
  output Carry
);

  wire adder_1_c, adder_2_c, adder_3_c;

  Adder adder_1 (.X(A1), .Y(B1), .Z(_0), .S(S1), .C(adder_1_c));
  Adder adder_2 (.X(A2), .Y(B2), .Z(adder_1_c), .S(S2), .C(adder_2_c));
  Adder adder_3 (.X(A3), .Y(B3), .Z(adder_2_c), .S(S3), .C(adder_3_c));
  Adder adder_4 (.X(A4), .Y(B4), .Z(adder_3_c), .S(S4), .C(Carry));
endmodule
